# Fritzing sketch tonnetzWandSchematic (saved by Fritzing 0.9.3b)
breadboards: 1

parts:
  TonnetzWand = Arduino Uno (Rev3)
  Radio_Transmitter = NRF24L01+ Breakout Board
  Wii_Nunchuk = IC, DIP package, 6 pins [chip_label=Nunchuk]

nets:
  N1: TonnetzWand.D8, Radio_Transmitter.CS
  N2: TonnetzWand.D11_PWM/MOSI, Radio_Transmitter.MOSI
  N3: TonnetzWand.D12/MISO, Radio_Transmitter.MISO
  N4: TonnetzWand.D13/SCK, Radio_Transmitter.SCK
  GND: TonnetzWand.GND, Radio_Transmitter.GND
  N5: TonnetzWand.A4/SDA, Wii_Nunchuk.pin1
  N6: TonnetzWand.A5/SCL, Wii_Nunchuk.pin2
  N7: TonnetzWand.D7, Radio_Transmitter.CE
  3V3: TonnetzWand.3V3, Radio_Transmitter.VCC, Wii_Nunchuk.pin3

notes:
  SDA
  SCL
  3.3V
